// Logisim project MultiplexerOnly.circ as structural Verilog: 1 circuit, main circuit main
module main (
  input  A,
  input  C,
  input  B,
  output Y
);

  wire multiplexer_1_out, multiplexer_2_out, multiplexer_3_out, multiplexer_4_out;

  Multiplexer #(.enable("false")) multiplexer_1 (.in0(C), .in1(A), .out(multiplexer_1_out), .sel(A));
  Multiplexer #(.enable("false")) multiplexer_2 (.in0(C), .in1(A), .out(multiplexer_2_out), .sel(C));
  Multiplexer #(.enable("false")) multiplexer_3 (
    .in0(1'b1), .in1(1'b0), .out(multiplexer_3_out), .sel(multiplexer_1_out));
  Multiplexer #(.enable("false")) multiplexer_4 (.in0(multiplexer_2_out), .in1(1'b0), .out(multiplexer_4_out), .sel(B));
  Multiplexer #(.enable("false")) multiplexer_5 (.in0(multiplexer_3_out), .in1(1'b1), .out(Y), .sel(multiplexer_4_out));
endmodule
